// Logisim project main.circ as structural Verilog: 14 circuits, main circuit main
module main (
  input  [7:0] in_1,
  input  in_2,
  input  in_3
);

  wire clock_1_out;
  wire [7:0] display_driver_1_out_5, display_driver_1_out_6, display_driver_1_out_7, display_driver_1_out_8,
       display_driver_1_out_9, display_driver_1_out_10, display_driver_1_out_11, display_driver_1_out_12,
       display_driver_1_out_13, display_driver_1_out_14, display_driver_1_out_15, display_driver_1_out_16,
       display_driver_1_out_17, display_driver_1_out_18, display_driver_1_out_19, display_driver_1_out_20,
       display_driver_1_out_21, display_driver_1_out_22, display_driver_1_out_23, display_driver_1_out_24,
       display_driver_1_out_25, display_driver_1_out_26, display_driver_1_out_27, display_driver_1_out_28,
       display_driver_1_out_29, display_driver_1_out_30, display_driver_1_out_31, display_driver_1_out_32,
       display_driver_1_out_33, display_driver_1_out_34, display_driver_1_out_35, display_driver_1_out_36;

  Clock clock_1 (.out(clock_1_out));
  DotMatrix #(.matrixcols(32), .matrixrows(8)) dotmatrix_1 (
    .col0(display_driver_1_out_5), .col1(display_driver_1_out_6), .col2(display_driver_1_out_7),
    .col3(display_driver_1_out_8), .col4(display_driver_1_out_9), .col5(display_driver_1_out_10),
    .col6(display_driver_1_out_11), .col7(display_driver_1_out_12), .col8(display_driver_1_out_13),
    .col9(display_driver_1_out_14), .col10(display_driver_1_out_15), .col11(display_driver_1_out_16),
    .col12(display_driver_1_out_17), .col13(display_driver_1_out_18), .col14(display_driver_1_out_19),
    .col15(display_driver_1_out_20), .col16(display_driver_1_out_21), .col17(display_driver_1_out_22),
    .col18(display_driver_1_out_23), .col19(display_driver_1_out_24), .col20(display_driver_1_out_25),
    .col21(display_driver_1_out_26), .col22(display_driver_1_out_27), .col23(display_driver_1_out_28),
    .col24(display_driver_1_out_29), .col25(display_driver_1_out_30), .col26(display_driver_1_out_31),
    .col27(display_driver_1_out_32), .col28(display_driver_1_out_33), .col29(display_driver_1_out_34),
    .col30(display_driver_1_out_35), .col31(display_driver_1_out_36));
  display_driver display_driver_1 (
    .in_1(in_1), .in_2(clock_1_out), .in_3(in_2), .in_4(in_3), .out_5(display_driver_1_out_5),
    .out_6(display_driver_1_out_6), .out_7(display_driver_1_out_7), .out_8(display_driver_1_out_8),
    .out_9(display_driver_1_out_9), .out_10(display_driver_1_out_10), .out_11(display_driver_1_out_11),
    .out_12(display_driver_1_out_12), .out_13(display_driver_1_out_13), .out_14(display_driver_1_out_14),
    .out_15(display_driver_1_out_15), .out_16(display_driver_1_out_16), .out_17(display_driver_1_out_17),
    .out_18(display_driver_1_out_18), .out_19(display_driver_1_out_19), .out_20(display_driver_1_out_20),
    .out_21(display_driver_1_out_21), .out_22(display_driver_1_out_22), .out_23(display_driver_1_out_23),
    .out_24(display_driver_1_out_24), .out_25(display_driver_1_out_25), .out_26(display_driver_1_out_26),
    .out_27(display_driver_1_out_27), .out_28(display_driver_1_out_28), .out_29(display_driver_1_out_29),
    .out_30(display_driver_1_out_30), .out_31(display_driver_1_out_31), .out_32(display_driver_1_out_32),
    .out_33(display_driver_1_out_33), .out_34(display_driver_1_out_34), .out_35(display_driver_1_out_35),
    .out_36(display_driver_1_out_36));
endmodule

module _8bit_register (
  input  in_1,
  input  [7:0] in_2,
  input  [1:0] in_3,
  input  in_4,
  output [7:0] out_5,
  output [7:0] out_6
);

  wire and_1_out;

  Pull_Resistor pull_resistor_1 (.node(in_3));
  Pull_Resistor pull_resistor_2 (.node(in_4));
  and and_1 (and_1_out, in_1, in_3[0]);
  D_Flip_Flop #(.trigger("high")) d_ff_1 (
    .clk(and_1_out), .D(in_2[0]), .Q(out_5[0]), .reset(in_4));  // open: Qn, preset, en
  D_Flip_Flop #(.trigger("high")) d_ff_2 (
    .clk(and_1_out), .D(in_2[1]), .Q(out_5[1]), .reset(in_4));  // open: Qn, preset, en
  D_Flip_Flop #(.trigger("high")) d_ff_3 (
    .clk(and_1_out), .D(in_2[2]), .Q(out_5[2]), .reset(in_4));  // open: Qn, preset, en
  D_Flip_Flop #(.trigger("high")) d_ff_4 (
    .clk(and_1_out), .D(in_2[3]), .Q(out_5[3]), .reset(in_4));  // open: Qn, preset, en
  D_Flip_Flop #(.trigger("high")) d_ff_5 (
    .clk(and_1_out), .D(in_2[4]), .Q(out_5[4]), .reset(in_4));  // open: Qn, preset, en
  D_Flip_Flop #(.trigger("high")) d_ff_6 (
    .clk(and_1_out), .D(in_2[5]), .Q(out_5[5]), .reset(in_4));  // open: Qn, preset, en
  D_Flip_Flop #(.trigger("high")) d_ff_7 (
    .clk(and_1_out), .D(in_2[6]), .Q(out_5[6]), .reset(in_4));  // open: Qn, preset, en
  D_Flip_Flop #(.trigger("high")) d_ff_8 (
    .clk(and_1_out), .D(in_2[7]), .Q(out_5[7]), .reset(in_4));  // open: Qn, preset, en
  assign out_6 = in_3[1] ? out_5 : 8'bz;  // Controlled_Buffer controlled_buffer_1
endmodule

module Instruction_Pointer (
  input  in_1,
  input  [7:0] in_2,
  input  [7:0] HIGH,
  input  [4:0] in_4,
  input  in_5,
  output [15:0] out_6,
  output [7:0] LOW2DB,
  output [7:0] LOW2AB,
  output [7:0] HIGH2AB,
  output [7:0] HIGH2DB
);

  wire n2_bit_counter_1_out_9, n2_bit_counter_2_out_9, n2_bit_counter_3_out_9, n2_bit_counter_4_out_9,
       n2_bit_counter_5_out_9, n2_bit_counter_6_out_9, n2_bit_counter_7_out_9;

  Pull_Resistor pull_resistor_1 (.node(in_4));
  Pull_Resistor pull_resistor_2 (.node(in_2));
  Pull_Resistor pull_resistor_3 (.node(HIGH));
  Pull_Resistor pull_resistor_4 (.node(in_1));
  Pull_Resistor pull_resistor_5 (.node(in_5));
  _2_bit_counter u_2_bit_counter_1 (
    .clk(in_1), .enable(in_4[0]), .d1(in_2[0]), .d2(in_2[1]), .inp_count(in_4[1]), .reset(in_5),
    .out_7(out_6[0]), .out_8(out_6[1]), .out_9(n2_bit_counter_1_out_9));
  _2_bit_counter u_2_bit_counter_2 (
    .clk(in_1), .enable(n2_bit_counter_1_out_9), .d1(in_2[2]), .d2(in_2[3]), .inp_count(in_4[1]),
    .reset(in_5), .out_7(out_6[2]), .out_8(out_6[3]), .out_9(n2_bit_counter_2_out_9));
  _2_bit_counter u_2_bit_counter_3 (
    .clk(in_1), .enable(n2_bit_counter_2_out_9), .d1(in_2[4]), .d2(in_2[5]), .inp_count(in_4[1]),
    .reset(in_5), .out_7(out_6[4]), .out_8(out_6[5]), .out_9(n2_bit_counter_3_out_9));
  _2_bit_counter u_2_bit_counter_4 (
    .clk(in_1), .enable(n2_bit_counter_3_out_9), .d1(in_2[6]), .d2(in_2[7]), .inp_count(in_4[1]),
    .reset(in_5), .out_7(out_6[6]), .out_8(out_6[7]), .out_9(n2_bit_counter_4_out_9));
  _2_bit_counter u_2_bit_counter_5 (
    .clk(in_1), .enable(n2_bit_counter_4_out_9), .d1(HIGH[0]), .d2(HIGH[1]), .inp_count(in_4[1]),
    .reset(in_5), .out_7(out_6[8]), .out_8(out_6[9]), .out_9(n2_bit_counter_5_out_9));
  _2_bit_counter u_2_bit_counter_6 (
    .clk(in_1), .enable(n2_bit_counter_5_out_9), .d1(HIGH[2]), .d2(HIGH[3]), .inp_count(in_4[1]),
    .reset(in_5), .out_7(out_6[10]), .out_8(out_6[11]), .out_9(n2_bit_counter_6_out_9));
  _2_bit_counter u_2_bit_counter_7 (
    .clk(in_1), .enable(n2_bit_counter_6_out_9), .d1(HIGH[4]), .d2(HIGH[5]), .inp_count(in_4[1]),
    .reset(in_5), .out_7(out_6[12]), .out_8(out_6[13]), .out_9(n2_bit_counter_7_out_9));
  _2_bit_counter u_2_bit_counter_8 (
    .clk(in_1), .enable(n2_bit_counter_7_out_9), .d1(HIGH[6]), .d2(HIGH[7]), .inp_count(in_4[1]),
    .reset(in_5), .out_7(out_6[14]), .out_8(out_6[15]));  // open: out_9
  assign LOW2DB = in_4[3] ? out_6[7:0] : 8'bz;  // Controlled_Buffer controlled_buffer_1
  assign LOW2AB = in_4[2] ? out_6[7:0] : 8'bz;  // Controlled_Buffer controlled_buffer_2
  assign HIGH2AB = in_4[2] ? out_6[15:8] : 8'bz;  // Controlled_Buffer controlled_buffer_3
  assign HIGH2DB = in_4[4] ? out_6[15:8] : 8'bz;  // Controlled_Buffer controlled_buffer_4

  // Other names for the same wires on the sheet: en = in_4[0]; L2DB = in_4[3]; H2DB = in_4[4]

  // Notes on the sheet:
  //   LOW
endmodule

module _2_bit_counter (
  input  clk,
  input  enable,
  input  d1,
  input  d2,
  input  inp_count,
  input  reset,
  output out_7,
  output out_8,
  output out_9
);

  wire and_1_out, and_2_out, d_ff_1_qn, multiplexer_1_out, multiplexer_2_out, or_1_out, xor_1_out;

  and and_1 (and_1_out, inp_count, clk);
  or or_1 (or_1_out, and_1_out, and_2_out);
  and and_2 (and_2_out, clk, enable);
  Multiplexer #(.enable("false")) multiplexer_1 (.in0(d_ff_1_qn), .in1(d1), .out(multiplexer_1_out), .sel(inp_count));
  D_Flip_Flop #(.trigger("falling")) d_ff_1 (
    .clk(or_1_out), .D(multiplexer_1_out), .Q(out_7), .Qn(d_ff_1_qn), .reset(reset));  // open: preset, en
  xor xor_1 (xor_1_out, out_7, out_8);
  Multiplexer #(.enable("false")) multiplexer_2 (.in0(xor_1_out), .in1(d2), .out(multiplexer_2_out), .sel(inp_count));
  D_Flip_Flop #(.trigger("falling")) d_ff_2 (
    .clk(or_1_out), .D(multiplexer_2_out), .Q(out_8), .reset(reset));  // open: Qn, preset, en
  and and_3 (out_9, out_7, enable, out_8);
endmodule

module ALU (
  input  [7:0] in_1,
  input  clk,
  input  [7:0] in_3,
  input  [6:0] in_4,
  output [7:0] out_5,
  output [1:0] out_6
);

  wire and_2_out, cf, not_1_out, not_2_out, not_3_out, not_4_out, zf;
  wire [7:0] and_1_out, full_adder_8bit_1_out_3, multiplexer_1_out, multiplexer_3_out, pull_resistor_3_node,
       xnor_1_out, xnor_9_out, xnor_17_out;

  Pull_Resistor pull_resistor_1 (.node(in_4));
  Multiplexer #(.width(8), .enable("false")) multiplexer_1 (
    .in0(in_1), .in1({8{1'b0}}), .out(multiplexer_1_out), .sel(in_4[0]));
  Pull_Resistor pull_resistor_2 (.node(multiplexer_1_out));
  Pull_Resistor pull_resistor_3 (.node(pull_resistor_3_node));
  Multiplexer #(.width(8), .enable("false")) multiplexer_2 (
    .in0(in_3), .in1({8{1'b0}}), .out(pull_resistor_3_node), .sel(in_4[2]));
  not not_1 (not_1_out, in_4[1]);
  not not_2 (not_2_out, in_4[3]);
  xnor xnor_1 (xnor_1_out[0], multiplexer_1_out[0], not_1_out);
  xnor xnor_2 (xnor_1_out[1], multiplexer_1_out[1], not_1_out);
  xnor xnor_3 (xnor_1_out[2], multiplexer_1_out[2], not_1_out);
  xnor xnor_4 (xnor_1_out[3], multiplexer_1_out[3], not_1_out);
  xnor xnor_5 (xnor_1_out[4], multiplexer_1_out[4], not_1_out);
  xnor xnor_6 (xnor_1_out[5], multiplexer_1_out[5], not_1_out);
  xnor xnor_7 (xnor_1_out[6], multiplexer_1_out[6], not_1_out);
  xnor xnor_8 (xnor_1_out[7], multiplexer_1_out[7], not_1_out);
  xnor xnor_9 (xnor_9_out[0], pull_resistor_3_node[0], not_2_out);
  xnor xnor_10 (xnor_9_out[1], pull_resistor_3_node[1], not_2_out);
  xnor xnor_11 (xnor_9_out[2], pull_resistor_3_node[2], not_2_out);
  xnor xnor_12 (xnor_9_out[3], pull_resistor_3_node[3], not_2_out);
  xnor xnor_13 (xnor_9_out[4], pull_resistor_3_node[4], not_2_out);
  xnor xnor_14 (xnor_9_out[5], pull_resistor_3_node[5], not_2_out);
  xnor xnor_15 (xnor_9_out[6], pull_resistor_3_node[6], not_2_out);
  xnor xnor_16 (xnor_9_out[7], pull_resistor_3_node[7], not_2_out);
  full_adder_8bit full_adder_8bit_1 (.in_1(xnor_1_out), .in_2(xnor_9_out), .out_3(full_adder_8bit_1_out_3), .out_4(cf));
  assign and_1_out = xnor_1_out & xnor_9_out;  // AND_Gate and_1, 8 bits wide
  Multiplexer #(.width(8), .enable("false")) multiplexer_3 (
    .in0(full_adder_8bit_1_out_3), .in1(and_1_out), .out(multiplexer_3_out), .sel(in_4[4]));
  not not_3 (not_3_out, in_4[5]);
  xnor xnor_17 (xnor_17_out[0], multiplexer_3_out[0], not_3_out);
  xnor xnor_18 (xnor_17_out[1], multiplexer_3_out[1], not_3_out);
  xnor xnor_19 (xnor_17_out[2], multiplexer_3_out[2], not_3_out);
  xnor xnor_20 (xnor_17_out[3], multiplexer_3_out[3], not_3_out);
  xnor xnor_21 (xnor_17_out[4], multiplexer_3_out[4], not_3_out);
  xnor xnor_22 (xnor_17_out[5], multiplexer_3_out[5], not_3_out);
  xnor xnor_23 (xnor_17_out[6], multiplexer_3_out[6], not_3_out);
  xnor xnor_24 (xnor_17_out[7], multiplexer_3_out[7], not_3_out);
  not not_4 (not_4_out, clk);
  nor nor_1 (zf, xnor_17_out[0], xnor_17_out[1], xnor_17_out[2], xnor_17_out[3], xnor_17_out[4], xnor_17_out[5], xnor_17_out[6], xnor_17_out[7]);
  _8bit_register u_8bit_register_1 (
    .in_1(not_4_out), .out_5(out_5), .in_2(xnor_17_out), .in_3(2'b01), .in_4(1'b0));  // open: out_6
  and and_2 (and_2_out, clk, in_4[6]);
  D_Flip_Flop d_ff_1 (.clk(and_2_out), .D(zf), .Q(out_6[0]));  // open: Qn, preset, en, reset
  D_Flip_Flop d_ff_2 (.clk(and_2_out), .D(cf), .Q(out_6[1]));  // open: Qn, preset, en, reset
endmodule

module full_adder (
  input  in_1,
  input  in_2,
  input  in_3,
  output out_4,
  output out_5
);

  wire nor_1_out, nor_2_out, xnor_1_out;

  nor nor_1 (nor_1_out, in_1, in_2);
  xnor xnor_1 (xnor_1_out, in_1, in_2);
  nor nor_2 (nor_2_out, xnor_1_out, in_3);
  xnor xnor_2 (out_4, xnor_1_out, in_3);
  nor nor_3 (out_5, nor_1_out, nor_2_out);
endmodule

module full_adder_8bit (
  input  [7:0] in_1,
  input  [7:0] in_2,
  output [7:0] out_3,
  output out_4
);

  wire full_adder_1_out_5, full_adder_2_out_5, full_adder_3_out_5, full_adder_4_out_5, full_adder_5_out_5,
       full_adder_6_out_5, full_adder_7_out_5;

  Pull_Resistor pull_resistor_1 (.node(in_1));
  Pull_Resistor pull_resistor_2 (.node(in_2));
  full_adder full_adder_1 (.in_1(in_1[0]), .in_2(in_2[0]), .in_3(1'b0), .out_4(out_3[0]), .out_5(full_adder_1_out_5));
  full_adder full_adder_2 (
    .in_1(in_1[1]), .in_2(in_2[1]), .in_3(full_adder_1_out_5), .out_4(out_3[1]), .out_5(full_adder_2_out_5));
  full_adder full_adder_3 (
    .in_1(in_1[2]), .in_2(in_2[2]), .in_3(full_adder_2_out_5), .out_4(out_3[2]), .out_5(full_adder_3_out_5));
  full_adder full_adder_4 (
    .in_1(in_1[3]), .in_2(in_2[3]), .in_3(full_adder_3_out_5), .out_4(out_3[3]), .out_5(full_adder_4_out_5));
  full_adder full_adder_5 (
    .in_1(in_1[4]), .in_2(in_2[4]), .in_3(full_adder_4_out_5), .out_4(out_3[4]), .out_5(full_adder_5_out_5));
  full_adder full_adder_6 (
    .in_1(in_1[5]), .in_2(in_2[5]), .in_3(full_adder_5_out_5), .out_4(out_3[5]), .out_5(full_adder_6_out_5));
  full_adder full_adder_7 (
    .in_1(in_1[6]), .in_2(in_2[6]), .in_3(full_adder_6_out_5), .out_4(out_3[6]), .out_5(full_adder_7_out_5));
  full_adder full_adder_8 (.in_1(in_1[7]), .in_2(in_2[7]), .in_3(full_adder_7_out_5), .out_4(out_3[7]), .out_5(out_4));
endmodule

module falling_edge_regester (
  input  in_1,
  input  [7:0] in_2,
  input  in_3,
  output [7:0] out_4
);

  Pull_Resistor pull_resistor_1 (.node(in_2));
  Pull_Resistor pull_resistor_2 (.node(in_3));
  D_Flip_Flop #(.trigger("falling")) d_ff_1 (
    .clk(in_1), .D(in_2[0]), .Q(out_4[0]), .reset(in_3));  // open: Qn, preset, en
  D_Flip_Flop #(.trigger("falling")) d_ff_2 (
    .clk(in_1), .D(in_2[1]), .Q(out_4[1]), .reset(in_3));  // open: Qn, preset, en
  D_Flip_Flop #(.trigger("falling")) d_ff_3 (
    .clk(in_1), .D(in_2[2]), .Q(out_4[2]), .reset(in_3));  // open: Qn, preset, en
  D_Flip_Flop #(.trigger("falling")) d_ff_4 (
    .clk(in_1), .D(in_2[3]), .Q(out_4[3]), .reset(in_3));  // open: Qn, preset, en
  D_Flip_Flop #(.trigger("falling")) d_ff_5 (
    .clk(in_1), .D(in_2[4]), .Q(out_4[4]), .reset(in_3));  // open: Qn, preset, en
  D_Flip_Flop #(.trigger("falling")) d_ff_6 (
    .clk(in_1), .D(in_2[5]), .Q(out_4[5]), .reset(in_3));  // open: Qn, preset, en
  D_Flip_Flop #(.trigger("falling")) d_ff_7 (
    .clk(in_1), .D(in_2[6]), .Q(out_4[6]), .reset(in_3));  // open: Qn, preset, en
  D_Flip_Flop #(.trigger("falling")) d_ff_8 (
    .clk(in_1), .D(in_2[7]), .Q(out_4[7]), .reset(in_3));  // open: Qn, preset, en
endmodule

module Stack_Pointer (
  input  in_1,
  input  [7:0] in_2,
  input  [1:0] in_3,
  input  in_4,
  output [7:0] out_5,
  output [7:0] out_6,
  output [7:0] out_7
);

  wire and_1_out;

  and and_1 (and_1_out, in_1, in_3[0]);
  Pull_Resistor pull_resistor_1 (.node(in_2));
  D_Flip_Flop #(.trigger("high")) d_ff_1 (
    .clk(and_1_out), .D(in_2[0]), .Q(out_5[0]), .preset(in_4));  // open: Qn, en, reset
  D_Flip_Flop #(.trigger("high")) d_ff_2 (
    .clk(and_1_out), .D(in_2[1]), .Q(out_5[1]), .preset(in_4));  // open: Qn, en, reset
  D_Flip_Flop #(.trigger("high")) d_ff_3 (
    .clk(and_1_out), .D(in_2[2]), .Q(out_5[2]), .preset(in_4));  // open: Qn, en, reset
  D_Flip_Flop #(.trigger("high")) d_ff_4 (
    .clk(and_1_out), .D(in_2[3]), .Q(out_5[3]), .preset(in_4));  // open: Qn, en, reset
  D_Flip_Flop #(.trigger("high")) d_ff_5 (
    .clk(and_1_out), .D(in_2[4]), .Q(out_5[4]), .preset(in_4));  // open: Qn, en, reset
  D_Flip_Flop #(.trigger("high")) d_ff_6 (
    .clk(and_1_out), .D(in_2[5]), .Q(out_5[5]), .preset(in_4));  // open: Qn, en, reset
  D_Flip_Flop #(.trigger("high")) d_ff_7 (
    .clk(and_1_out), .D(in_2[6]), .Q(out_5[6]), .preset(in_4));  // open: Qn, en, reset
  D_Flip_Flop #(.trigger("high")) d_ff_8 (
    .clk(and_1_out), .D(in_2[7]), .Q(out_5[7]), .preset(in_4));  // open: Qn, en, reset
  assign out_6 = in_3[1] ? out_5 : 8'bz;  // Controlled_Buffer controlled_buffer_1
  Pull_Resistor pull_resistor_2 (.node(in_3[1]));
  assign out_7 = in_3[1] ? {8{1'b1}} : 8'bz;  // Controlled_Buffer controlled_buffer_2
endmodule

module Address_Latch (
  input  in_1,
  input  [7:0] in_2,
  input  [2:0] in_3,
  input  in_4,
  output [7:0] out_5,
  output [7:0] out_6,
  output [7:0] out_7,
  output [7:0] out_8
);

  wire and_1_out, and_2_out;

  Pull_Resistor pull_resistor_1 (.node(in_3));
  Pull_Resistor pull_resistor_2 (.node(in_4));
  Pull_Resistor pull_resistor_3 (.node(in_2));
  Pull_Resistor pull_resistor_4 (.node(in_2));
  and and_1 (and_1_out, in_1, in_3[0]);
  and and_2 (and_2_out, in_1, in_3[1]);
  D_Flip_Flop #(.trigger("high")) d_ff_1 (
    .clk(and_1_out), .D(in_2[0]), .Q(out_5[0]), .reset(in_4));  // open: Qn, preset, en
  D_Flip_Flop #(.trigger("high")) d_ff_2 (
    .clk(and_1_out), .D(in_2[1]), .Q(out_5[1]), .reset(in_4));  // open: Qn, preset, en
  D_Flip_Flop #(.trigger("high")) d_ff_3 (
    .clk(and_1_out), .D(in_2[2]), .Q(out_5[2]), .reset(in_4));  // open: Qn, preset, en
  D_Flip_Flop #(.trigger("high")) d_ff_4 (
    .clk(and_1_out), .D(in_2[3]), .Q(out_5[3]), .reset(in_4));  // open: Qn, preset, en
  D_Flip_Flop #(.trigger("high")) d_ff_5 (
    .clk(and_1_out), .D(in_2[4]), .Q(out_5[4]), .reset(in_4));  // open: Qn, preset, en
  D_Flip_Flop #(.trigger("high")) d_ff_6 (
    .clk(and_1_out), .D(in_2[5]), .Q(out_5[5]), .reset(in_4));  // open: Qn, preset, en
  D_Flip_Flop #(.trigger("high")) d_ff_7 (
    .clk(and_1_out), .D(in_2[6]), .Q(out_5[6]), .reset(in_4));  // open: Qn, preset, en
  D_Flip_Flop #(.trigger("high")) d_ff_8 (
    .clk(and_1_out), .D(in_2[7]), .Q(out_5[7]), .reset(in_4));  // open: Qn, preset, en
  D_Flip_Flop #(.trigger("high")) d_ff_9 (
    .clk(and_2_out), .D(in_2[0]), .Q(out_7[0]), .reset(in_4));  // open: Qn, preset, en
  D_Flip_Flop #(.trigger("high")) d_ff_10 (
    .clk(and_2_out), .D(in_2[1]), .Q(out_7[1]), .reset(in_4));  // open: Qn, preset, en
  D_Flip_Flop #(.trigger("high")) d_ff_11 (
    .clk(and_2_out), .D(in_2[2]), .Q(out_7[2]), .reset(in_4));  // open: Qn, preset, en
  D_Flip_Flop #(.trigger("high")) d_ff_12 (
    .clk(and_2_out), .D(in_2[3]), .Q(out_7[3]), .reset(in_4));  // open: Qn, preset, en
  D_Flip_Flop #(.trigger("high")) d_ff_13 (
    .clk(and_2_out), .D(in_2[4]), .Q(out_7[4]), .reset(in_4));  // open: Qn, preset, en
  D_Flip_Flop #(.trigger("high")) d_ff_14 (
    .clk(and_2_out), .D(in_2[5]), .Q(out_7[5]), .reset(in_4));  // open: Qn, preset, en
  D_Flip_Flop #(.trigger("high")) d_ff_15 (
    .clk(and_2_out), .D(in_2[6]), .Q(out_7[6]), .reset(in_4));  // open: Qn, preset, en
  D_Flip_Flop #(.trigger("high")) d_ff_16 (
    .clk(and_2_out), .D(in_2[7]), .Q(out_7[7]), .reset(in_4));  // open: Qn, preset, en
  assign out_6 = in_3[2] ? out_5 : 8'bz;  // Controlled_Buffer controlled_buffer_1
  assign out_8 = in_3[2] ? out_7 : 8'bz;  // Controlled_Buffer controlled_buffer_2

  // Other names for the same wires on the sheet: ALU_DB[7:0] = in_2; clk = in_1; High_Inp = in_3[0];
  //   LOW_Inp = in_3[1]; Out = in_3[2]
endmodule

module Instruction_Regester (
  input  [1:0] in_1,
  input  [7:0] in_2,
  input  in_3,
  input  Reset,
  output [6:0] out_5,
  output [1:0] A,
  output [1:0] x,
  output [1:0] sp,
  output [4:0] IP,
  output [2:0] Adress_Latch,
  output [2:0] RAM,
  output const_out,
  output [1:0] out_13
);

  wire d_ff_1_q, d_ff_2_qn, d_ff_3_qn, d_ff_4_qn, IR_RESET, multiplexer_1_out, nor_1_out, not_1_out;
  wire [7:0] falling_edge_regester_1_out_4;
  wire [12:10] d_ff_2_q;

  Pull_Resistor pull_resistor_1 (.node(IR_RESET));
  not not_1 (not_1_out, IR_RESET);
  Multiplexer #(.enable("false")) multiplexer_1 (.in0(d_ff_1_q), .in1(1'b1), .out(multiplexer_1_out), .sel(Reset));
  D_Flip_Flop #(.trigger("falling")) d_ff_1 (
    .clk(in_3), .D(IR_RESET), .Q(d_ff_1_q), .reset(not_1_out));  // open: Qn, preset, en
  D_Flip_Flop #(.trigger("falling")) d_ff_2 (
    .clk(in_3), .D(d_ff_2_qn), .Q(d_ff_2_q[10]), .Qn(d_ff_2_qn), .reset(multiplexer_1_out));  // open: preset, en
  D_Flip_Flop #(.trigger("falling")) d_ff_3 (
    .clk(d_ff_2_q[10]), .D(d_ff_3_qn), .Q(d_ff_2_q[11]), .Qn(d_ff_3_qn), .reset(multiplexer_1_out));  // open: preset, en
  nor nor_1 (nor_1_out, d_ff_2_q[10], d_ff_2_q[11], d_ff_2_q[12], ~in_3);  // NOR_Gate
  D_Flip_Flop #(.trigger("falling")) d_ff_4 (
    .clk(d_ff_2_q[11]), .D(d_ff_4_qn), .Q(d_ff_2_q[12]), .Qn(d_ff_4_qn), .reset(multiplexer_1_out));  // open: preset, en
  falling_edge_regester falling_edge_regester_1 (
    .in_1(nor_1_out), .in_2(in_2), .in_3(Reset), .out_4(falling_edge_regester_1_out_4));
  ROM #(.addrWidth(13), .dataWidth(28)) rom_1 (
    .addr({d_ff_2_q, falling_edge_regester_1_out_4, in_1}),
    .data({out_13, IR_RESET, const_out, RAM, Adress_Latch, IP, sp, x, A, out_5}), .sel(1'b1));

  // Notes on the sheet:
  //   contents of rom_1 (hex, n*v repeats v):
  //   1024*80a000 4*2000000 4*280a081 4*280a201 4*2000301 4*2000481 16*84a001 4*484a040 4*20004c0
  //   4*2000640 4*280a0c0 4*680a240 8*84a001 4*20004e2 4*6000362 4*280a0e2 4*680a262 16*84a001 4*881001
  //   2000 2000 84a001 84a001 2000 84a001 2000 84a001 4*2000462 4*6000162 4*280a062 4*680a062 12*84a001
  //   4*2500400 904*0 18*88a001 88a02b 88a02b 16*0 8*88a001 16*0 16*88a001 4*800180c 2002000 2002000
  //   88a001 88a001 2002000 88a001 2002000 88a001 16*0 8*88a001 4*2500100 908*0 4*2300100 4*2300400
  //   4*2900081 4*2900201 4*2900081 16*0 4*29000c0 4*6900240 16*0 4*29000e2 4*6900262 4*2106000 4*821182e
  //   4*841001 0 0 2106000 2106000 0 2106000 0 2106000 16*0 4*2900062 4*6900062 4*84a001 944*0 4*84a001
  //   32*0 4*822182e 4*a10680c 980*0 4*88a001 32*0 4*2106000 984*0 4*29000c0
  //   ALU
endmodule

module Full_Arch (
  input  in_1
);

  wire clk, CONST_CB, INP_OUT, input_output_1_out_7, input_output_1_out_8, not_1_out, not_2_out, not_3_out;
  wire [1:0] ALU_MODE_SEL, Areg_CB, flags, SPreg_CB, Xreg_CB;
  wire [2:0] ALreg_CB, ROM_CB;
  wire [4:0] IPreg_CB;
  wire [6:0] ALU_CB;
  wire [7:0] A2ALU, address_latch_1_out_5, address_latch_1_out_7, ALU_bus, data_bus, display_driver_1_out_5,
       display_driver_1_out_6, display_driver_1_out_7, display_driver_1_out_8, display_driver_1_out_9,
       display_driver_1_out_10, display_driver_1_out_11, display_driver_1_out_12, display_driver_1_out_13,
       display_driver_1_out_14, display_driver_1_out_15, display_driver_1_out_16, display_driver_1_out_17,
       display_driver_1_out_18, display_driver_1_out_19, display_driver_1_out_20, display_driver_1_out_21,
       display_driver_1_out_22, display_driver_1_out_23, display_driver_1_out_24, display_driver_1_out_25,
       display_driver_1_out_26, display_driver_1_out_27, display_driver_1_out_28, display_driver_1_out_29,
       display_driver_1_out_30, display_driver_1_out_31, display_driver_1_out_32, display_driver_1_out_33,
       display_driver_1_out_34, display_driver_1_out_35, display_driver_1_out_36, High_AB,
       input_output_1_out_6, Low_AB, multiplexer_1_out, SP2ALU, X2ALU;
  wire [15:0] instruction_pointer_1_out_6;

  Instruction_Regester instruction_regester_1 (
    .in_1(flags), .in_2(data_bus), .in_3(clk), .out_5(ALU_CB), .A(Areg_CB), .x(Xreg_CB), .sp(SPreg_CB),
    .IP(IPreg_CB), .Adress_Latch(ALreg_CB), .RAM({ROM_CB[2], INP_OUT, ROM_CB[0]}), .const_out(CONST_CB),
    .out_13(ALU_MODE_SEL), .Reset(in_1));
  // Probe on address_latch_1_out_7
  // Probe on address_latch_1_out_5
  Address_Latch address_latch_1 (
    .in_1(clk), .in_2(ALU_bus), .in_3(ALreg_CB), .out_5(address_latch_1_out_5), .out_6(Low_AB),
    .out_7(address_latch_1_out_7), .out_8(High_AB), .in_4(in_1));
  _8bit_register u_8bit_register_1 (
    .in_1(clk), .out_6(data_bus), .out_5(A2ALU), .in_2(ALU_bus), .in_3(Areg_CB), .in_4(in_1));
  // Probe on A2ALU
  // Probe on SP2ALU
  Stack_Pointer stack_pointer_1 (
    .in_1(clk), .in_2(ALU_bus), .in_4(in_1), .out_5(SP2ALU), .out_6(Low_AB), .out_7(High_AB), .in_3(SPreg_CB));
  // Probe on instruction_pointer_1_out_6
  Instruction_Pointer instruction_pointer_1 (
    .in_1(clk), .HIGH2AB(High_AB), .in_5(in_1), .LOW2AB(Low_AB), .in_2(Low_AB), .HIGH(High_AB),
    .out_6(instruction_pointer_1_out_6), .in_4(IPreg_CB), .LOW2DB(data_bus), .HIGH2DB(data_bus));
  assign data_bus = CONST_CB ? 8'h2 : 8'bz;  // Controlled_Buffer controlled_buffer_1
  Pull_Resistor pull_resistor_1 (.node(CONST_CB));
  Clock clock_1 (.out(clk));
  _8bit_register u_8bit_register_2 (
    .in_1(clk), .out_6(data_bus), .out_5(X2ALU), .in_2(ALU_bus), .in_3(Xreg_CB), .in_4(in_1));
  // Probe on X2ALU
  Pull_Resistor pull_resistor_2 (.node({ROM_CB[2], INP_OUT, ROM_CB[0]}));
  Pull_Resistor pull_resistor_3 (.node({ROM_CB[2], INP_OUT, ROM_CB[0]}));
  Pull_Resistor pull_resistor_4 (.node(SPreg_CB));
  not not_1 (not_1_out, INP_OUT);
  Multiplexer #(.select(2), .width(8), .enable("false")) multiplexer_1 (
    .in0(A2ALU), .in1(X2ALU), .in2(SP2ALU), .in3({8{1'b0}}), .out(multiplexer_1_out), .sel(ALU_MODE_SEL));
  RAM #(.addrWidth(16), .bus("separate")) ram_1 (
    .addr({High_AB, Low_AB}), .din(data_bus), .data(data_bus), .str(ROM_CB[0]), .sel(not_1_out),
    .clk(not_2_out), .ld(ROM_CB[2]));  // open: clr
  not not_2 (not_2_out, clk);
  RAM #(.bus("separate")) ram_2 (
    .addr(Low_AB), .din(data_bus), .data(data_bus), .str(ROM_CB[0]), .sel(SPreg_CB[1]), .clk(not_3_out),
    .ld(1'b0), .clr(in_1));
  not not_3 (not_3_out, clk);
  ALU alu_1 (.in_1(multiplexer_1_out), .in_3(data_bus), .out_5(ALU_bus), .in_4(ALU_CB), .out_6(flags), .clk(clk));
  // Probe on ALU_bus
  input_output input_output_1 (
    .in_1(data_bus), .in_2(clk), .in_3(Low_AB), .enable(INP_OUT), .out_6(input_output_1_out_6),
    .out_7(input_output_1_out_7), .out_8(input_output_1_out_8), .in_5(in_1));  // open: out_9, out_10, out_11, out_12, out_13, out_14
  DotMatrix #(.matrixcols(32), .matrixrows(8)) dotmatrix_1 (
    .col0(display_driver_1_out_5), .col1(display_driver_1_out_6), .col2(display_driver_1_out_7),
    .col3(display_driver_1_out_8), .col4(display_driver_1_out_9), .col5(display_driver_1_out_10),
    .col6(display_driver_1_out_11), .col7(display_driver_1_out_12), .col8(display_driver_1_out_13),
    .col9(display_driver_1_out_14), .col10(display_driver_1_out_15), .col11(display_driver_1_out_16),
    .col12(display_driver_1_out_17), .col13(display_driver_1_out_18), .col14(display_driver_1_out_19),
    .col15(display_driver_1_out_20), .col16(display_driver_1_out_21), .col17(display_driver_1_out_22),
    .col18(display_driver_1_out_23), .col19(display_driver_1_out_24), .col20(display_driver_1_out_25),
    .col21(display_driver_1_out_26), .col22(display_driver_1_out_27), .col23(display_driver_1_out_28),
    .col24(display_driver_1_out_29), .col25(display_driver_1_out_30), .col26(display_driver_1_out_31),
    .col27(display_driver_1_out_32), .col28(display_driver_1_out_33), .col29(display_driver_1_out_34),
    .col30(display_driver_1_out_35), .col31(display_driver_1_out_36));
  display_driver display_driver_1 (
    .in_1(input_output_1_out_6), .in_2(input_output_1_out_7), .in_3(input_output_1_out_8), .in_4(in_1),
    .out_5(display_driver_1_out_5), .out_6(display_driver_1_out_6), .out_7(display_driver_1_out_7),
    .out_8(display_driver_1_out_8), .out_9(display_driver_1_out_9), .out_10(display_driver_1_out_10),
    .out_11(display_driver_1_out_11), .out_12(display_driver_1_out_12), .out_13(display_driver_1_out_13),
    .out_14(display_driver_1_out_14), .out_15(display_driver_1_out_15), .out_16(display_driver_1_out_16),
    .out_17(display_driver_1_out_17), .out_18(display_driver_1_out_18), .out_19(display_driver_1_out_19),
    .out_20(display_driver_1_out_20), .out_21(display_driver_1_out_21), .out_22(display_driver_1_out_22),
    .out_23(display_driver_1_out_23), .out_24(display_driver_1_out_24), .out_25(display_driver_1_out_25),
    .out_26(display_driver_1_out_26), .out_27(display_driver_1_out_27), .out_28(display_driver_1_out_28),
    .out_29(display_driver_1_out_29), .out_30(display_driver_1_out_30), .out_31(display_driver_1_out_31),
    .out_32(display_driver_1_out_32), .out_33(display_driver_1_out_33), .out_34(display_driver_1_out_34),
    .out_35(display_driver_1_out_35), .out_36(display_driver_1_out_36));

  // Other names for the same wires on the sheet: reset = in_1; ROM_CB[1] = INP_OUT

  // Notes on the sheet:
  //   A Register
  //   Stack Pointer
  //   Instruction Pointer
  //   constant out control
  //   X Register
  //   RAM&Stack
  //   Stack
endmodule

module display_driver (
  input  [7:0] in_1,
  input  in_2,
  input  in_3,
  input  in_4,
  output [7:0] out_5,
  output [7:0] out_6,
  output [7:0] out_7,
  output [7:0] out_8,
  output [7:0] out_9,
  output [7:0] out_10,
  output [7:0] out_11,
  output [7:0] out_12,
  output [7:0] out_13,
  output [7:0] out_14,
  output [7:0] out_15,
  output [7:0] out_16,
  output [7:0] out_17,
  output [7:0] out_18,
  output [7:0] out_19,
  output [7:0] out_20,
  output [7:0] out_21,
  output [7:0] out_22,
  output [7:0] out_23,
  output [7:0] out_24,
  output [7:0] out_25,
  output [7:0] out_26,
  output [7:0] out_27,
  output [7:0] out_28,
  output [7:0] out_29,
  output [7:0] out_30,
  output [7:0] out_31,
  output [7:0] out_32,
  output [7:0] out_33,
  output [7:0] out_34,
  output [7:0] out_35,
  output [7:0] out_36
);

  wire [7:0] shift_register_1_q0, shift_register_1_q1, shift_register_1_q2, shift_register_1_q3,
       shift_register_1_q4, shift_register_1_q5, shift_register_1_q6, shift_register_1_q7,
       shift_register_1_q8, shift_register_1_q9, shift_register_1_q10, shift_register_1_q11,
       shift_register_1_q12, shift_register_1_q13, shift_register_1_q14, shift_register_1_q15,
       shift_register_1_q16, shift_register_1_q17, shift_register_1_q18, shift_register_1_q19,
       shift_register_1_q20, shift_register_1_q21, shift_register_1_q22, shift_register_1_q23,
       shift_register_1_q24, shift_register_1_q25, shift_register_1_q26, shift_register_1_q27,
       shift_register_1_q28, shift_register_1_q29, shift_register_1_q30, shift_register_1_q31;

  Pull_Resistor pull_resistor_1 (.node(in_4));
  Shift_Register #(.width(8), .length(32), .trigger("falling")) shift_register_1 (
    .shift(1'b1), .in(in_1), .clk(in_2), .clr(in_4), .q0(shift_register_1_q0), .q1(shift_register_1_q1),
    .q2(shift_register_1_q2), .q3(shift_register_1_q3), .q4(shift_register_1_q4), .q5(shift_register_1_q5),
    .q6(shift_register_1_q6), .q7(shift_register_1_q7), .q8(shift_register_1_q8), .q9(shift_register_1_q9),
    .q10(shift_register_1_q10), .q11(shift_register_1_q11), .q12(shift_register_1_q12),
    .q13(shift_register_1_q13), .q14(shift_register_1_q14), .q15(shift_register_1_q15),
    .q16(shift_register_1_q16), .q17(shift_register_1_q17), .q18(shift_register_1_q18),
    .q19(shift_register_1_q19), .q20(shift_register_1_q20), .q21(shift_register_1_q21),
    .q22(shift_register_1_q22), .q23(shift_register_1_q23), .q24(shift_register_1_q24),
    .q25(shift_register_1_q25), .q26(shift_register_1_q26), .q27(shift_register_1_q27),
    .q28(shift_register_1_q28), .q29(shift_register_1_q29), .q30(shift_register_1_q30),
    .q31(shift_register_1_q31));  // open: out, load, d0, d1, d2, d3, d4, d5, d6, d7, d8, d9, d10, d11, d12, d13, d14, d15, d16, d17, d18, d19, d20, d21, d22, d23, d24, d25, d26, d27, d28, d29, d30, d31
  Register #(.trigger("high")) register_1 (.D(shift_register_1_q0), .Q(out_5), .clk(in_3), .clr(in_4));  // open: en
  Register #(.trigger("high")) register_2 (.D(shift_register_1_q1), .Q(out_6), .clk(in_3), .clr(in_4));  // open: en
  Register #(.trigger("high")) register_3 (.D(shift_register_1_q2), .Q(out_7), .clk(in_3), .clr(in_4));  // open: en
  Register #(.trigger("high")) register_4 (.D(shift_register_1_q3), .Q(out_8), .clk(in_3), .clr(in_4));  // open: en
  Register #(.trigger("high")) register_5 (.D(shift_register_1_q4), .Q(out_9), .clk(in_3), .clr(in_4));  // open: en
  Register #(.trigger("high")) register_6 (.D(shift_register_1_q5), .Q(out_10), .clk(in_3), .clr(in_4));  // open: en
  Register #(.trigger("high")) register_7 (.D(shift_register_1_q6), .Q(out_11), .clk(in_3), .clr(in_4));  // open: en
  Register #(.trigger("high")) register_8 (.D(shift_register_1_q7), .Q(out_12), .clk(in_3), .clr(in_4));  // open: en
  Register #(.trigger("high")) register_9 (.D(shift_register_1_q8), .Q(out_13), .clk(in_3), .clr(in_4));  // open: en
  Register #(.trigger("high")) register_10 (.D(shift_register_1_q9), .Q(out_14), .clk(in_3), .clr(in_4));  // open: en
  Register #(.trigger("high")) register_11 (.D(shift_register_1_q10), .Q(out_15), .clk(in_3), .clr(in_4));  // open: en
  Register #(.trigger("high")) register_12 (.D(shift_register_1_q11), .Q(out_16), .clk(in_3), .clr(in_4));  // open: en
  Register #(.trigger("high")) register_13 (.D(shift_register_1_q12), .Q(out_17), .clk(in_3), .clr(in_4));  // open: en
  Register #(.trigger("high")) register_14 (.D(shift_register_1_q13), .Q(out_18), .clk(in_3), .clr(in_4));  // open: en
  Register #(.trigger("high")) register_15 (.D(shift_register_1_q14), .Q(out_19), .clk(in_3), .clr(in_4));  // open: en
  Register #(.trigger("high")) register_16 (.D(shift_register_1_q15), .Q(out_20), .clk(in_3), .clr(in_4));  // open: en
  Register #(.trigger("high")) register_17 (.D(shift_register_1_q16), .Q(out_21), .clk(in_3), .clr(in_4));  // open: en
  Register #(.trigger("high")) register_18 (.D(shift_register_1_q17), .Q(out_22), .clk(in_3), .clr(in_4));  // open: en
  Register #(.trigger("high")) register_19 (.D(shift_register_1_q18), .Q(out_23), .clk(in_3), .clr(in_4));  // open: en
  Register #(.trigger("high")) register_20 (.D(shift_register_1_q19), .Q(out_24), .clk(in_3), .clr(in_4));  // open: en
  Register #(.trigger("high")) register_21 (.D(shift_register_1_q20), .Q(out_25), .clk(in_3), .clr(in_4));  // open: en
  Register #(.trigger("high")) register_22 (.D(shift_register_1_q21), .Q(out_26), .clk(in_3), .clr(in_4));  // open: en
  Register #(.trigger("high")) register_23 (.D(shift_register_1_q22), .Q(out_27), .clk(in_3), .clr(in_4));  // open: en
  Register #(.trigger("high")) register_24 (.D(shift_register_1_q23), .Q(out_28), .clk(in_3), .clr(in_4));  // open: en
  Register #(.trigger("high")) register_25 (.D(shift_register_1_q24), .Q(out_29), .clk(in_3), .clr(in_4));  // open: en
  Register #(.trigger("high")) register_26 (.D(shift_register_1_q25), .Q(out_30), .clk(in_3), .clr(in_4));  // open: en
  Register #(.trigger("high")) register_27 (.D(shift_register_1_q26), .Q(out_31), .clk(in_3), .clr(in_4));  // open: en
  Register #(.trigger("high")) register_28 (.D(shift_register_1_q27), .Q(out_32), .clk(in_3), .clr(in_4));  // open: en
  Register #(.trigger("high")) register_29 (.D(shift_register_1_q28), .Q(out_33), .clk(in_3), .clr(in_4));  // open: en
  Register #(.trigger("high")) register_30 (.D(shift_register_1_q29), .Q(out_34), .clk(in_3), .clr(in_4));  // open: en
  Register #(.trigger("high")) register_31 (.D(shift_register_1_q30), .Q(out_35), .clk(in_3), .clr(in_4));  // open: en
  Register #(.trigger("high")) register_32 (.D(shift_register_1_q31), .Q(out_36), .clk(in_3), .clr(in_4));  // open: en
  DotMatrix #(.matrixcols(32), .matrixrows(8)) dotmatrix_1 (
    .col0(out_5), .col1(out_6), .col2(out_7), .col3(out_8), .col4(out_9), .col5(out_10), .col6(out_11),
    .col7(out_12), .col8(out_13), .col9(out_14), .col10(out_15), .col11(out_16), .col12(out_17),
    .col13(out_18), .col14(out_19), .col15(out_20), .col16(out_21), .col17(out_22), .col18(out_23),
    .col19(out_24), .col20(out_25), .col21(out_26), .col22(out_27), .col23(out_28), .col24(out_29),
    .col25(out_30), .col26(out_31), .col27(out_32), .col28(out_33), .col29(out_34), .col30(out_35),
    .col31(out_36));
endmodule

module input_output (
  input  [7:0] in_1,
  input  in_2,
  input  [7:0] in_3,
  input  enable,
  input  in_5,
  output [7:0] out_6,
  output out_7,
  output out_8,
  output out_9,
  output out_10,
  output out_11,
  output out_12,
  output out_13,
  output out_14
);

  wire [0:0] and_1_out, and_2_out;

  Pull_Resistor pull_resistor_1 (.node(in_5));
  and and_1 (and_1_out[0], ~in_3[0], ~in_3[1], ~in_3[2], ~in_3[3], ~in_3[4], ~in_3[5], ~in_3[6], ~in_3[7], enable);  // AND_Gate
  and and_2 (and_2_out[0], in_3[0], ~in_3[1], ~in_3[2], ~in_3[3], ~in_3[4], ~in_3[5], ~in_3[6], ~in_3[7], enable);  // AND_Gate
  _8bit_register u_8bit_register_1 (
    .in_1(in_2), .out_5(out_6), .in_2(in_1), .in_3({1'b0, and_1_out[0]}), .in_4(in_5));  // open: out_6
  _8bit_register u_8bit_register_2 (
    .in_1(in_2), .out_5({out_14, out_13, out_12, out_11, out_10, out_9, out_8, out_7}), .in_2(in_1),
    .in_3({1'b0, and_2_out[0]}), .in_4(in_5));  // open: out_6

  // Other names for the same wires on the sheet: address_bus[7:0] = in_3; data_bus[7:0] = in_1
endmodule
